// Logisim project CRC.circ as structural Verilog: 1 circuit, main circuit main
module main (
  input  INPUT,
  input  CLK,
  input  CLEAR,
  output out_4
);

  wire j_k_ff_1_q, j_k_ff_1_qn, j_k_ff_2_q, j_k_ff_2_qn, j_k_ff_3_q, not_1_out, not_2_out, xor_1_out,
       xor_2_out;

  xor xor_1 (xor_1_out, out_4, INPUT);
  not not_1 (not_1_out, xor_1_out);
  J_K_Flip_Flop j_k_ff_1 (
    .J(xor_1_out), .clk(CLK), .K(not_1_out), .Q(j_k_ff_1_q), .Qn(j_k_ff_1_qn), .reset(CLEAR));  // open: preset, en
  J_K_Flip_Flop j_k_ff_2 (
    .J(j_k_ff_1_q), .clk(CLK), .K(j_k_ff_1_qn), .Q(j_k_ff_2_q), .Qn(j_k_ff_2_qn), .reset(CLEAR));  // open: preset, en
  xor xor_2 (xor_2_out, out_4, j_k_ff_3_q);
  J_K_Flip_Flop j_k_ff_3 (
    .J(j_k_ff_2_q), .clk(CLK), .K(j_k_ff_2_qn), .Q(j_k_ff_3_q), .reset(CLEAR));  // open: Qn, preset, en
  not not_2 (not_2_out, xor_2_out);
  J_K_Flip_Flop j_k_ff_4 (.J(xor_2_out), .clk(CLK), .K(not_2_out), .Q(out_4), .reset(CLEAR));  // open: Qn, preset, en
endmodule
