// Logisim project CRC_sec2.circ as structural Verilog: 1 circuit, main circuit main
module main (
  input  Input_data,
  input  CLK_pulse,
  input  CLR_clear_data,
  output Output
);

  wire j_k_ff_1_q, j_k_ff_2_q, j_k_ff_3_q, not_1_out, not_2_out, not_3_out, not_4_out, xor_1_out, xor_2_out;

  xor xor_1 (xor_1_out, Output, Input_data);
  J_K_Flip_Flop #(.trigger("falling")) j_k_ff_1 (
    .J(xor_1_out), .clk(CLK_pulse), .K(not_1_out), .Q(j_k_ff_1_q), .reset(CLR_clear_data));  // open: Qn, preset, en
  not not_1 (not_1_out, xor_1_out);
  xor xor_2 (xor_2_out, Output, j_k_ff_1_q);
  J_K_Flip_Flop #(.trigger("falling")) j_k_ff_2 (
    .J(xor_2_out), .clk(CLK_pulse), .K(not_2_out), .Q(j_k_ff_2_q), .reset(CLR_clear_data));  // open: Qn, preset, en
  not not_2 (not_2_out, xor_2_out);
  J_K_Flip_Flop #(.trigger("falling")) j_k_ff_3 (
    .J(j_k_ff_2_q), .clk(CLK_pulse), .K(not_3_out), .Q(j_k_ff_3_q), .reset(CLR_clear_data));  // open: Qn, preset, en
  not not_3 (not_3_out, j_k_ff_2_q);
  not not_4 (not_4_out, j_k_ff_3_q);
  J_K_Flip_Flop #(.trigger("falling")) j_k_ff_4 (
    .J(j_k_ff_3_q), .clk(CLK_pulse), .K(not_4_out), .Q(Output), .reset(CLR_clear_data));  // open: Qn, preset, en
endmodule
